# Fritzing sketch Nucleo-Groupe3V3 (saved by Fritzing 0.9.3b)
perfboards: 1

parts:
  EDGY_motor_control1 = EDGY
  R1 = PHOTOCELL [package=photocell]
  R2 = PHOTOCELL [package=photocell]
  R3 = PHOTOCELL [package=photocell]
  R4 = PHOTOCELL [package=photocell]
  R5 = PHOTOCELL [package=photocell]
  R6 = Resistor [tolerance=±5% resistance=220 package=THT]
  R7 = Resistor [tolerance=±5% resistance=220 package=THT]
  R8 = Resistor [tolerance=±5% resistance=220 package=THT]
  R9 = Resistor [tolerance=±5% resistance=220 package=THT]
  R10 = Resistor [tolerance=±5% resistance=220 package=THT]
  D1 = LTE-302 [package=lte-302]
  D2 = LTE-302 [package=lte-302]
  D3 = LTE-302 [package=lte-302]
  D4 = LTE-302 [package=lte-302]
  D5 = LTE-302 [package=lte-302]
  J1 = STM32 Nucleo boards
  U1 = ENCODER_2LED [package=encoder_led_2]
  M1 = DC Motor  # not connected
  M2 = DC Motor  # not connected
  U2 = LM2931_FIXED [package=dpak]
  VCC2 = 4 x AAA Battery Mount
  J3 = Infrared Proximity Sensor
  J2 = Infrared Proximity Sensor
  J4 = Infrared Proximity Sensor

nets:
  N1: EDGY_motor_control1.A1, EDGY_motor_control1.B1, VCC2.-
  N2: EDGY_motor_control1.Vin, J1.GND#1188
  N3: EDGY_motor_control1.A2, U1.SW
  N4: R1.P$1, R5.P$1, J1.GND#1189
  N5: R1.P$2, R10.Pin_1, J1.A0
  N6: R2.P$2, R7.Pin_1, J1.A1
  N7: R3.P$2, R8.Pin_1, D3.A, D3.C, J1.A2
  N8: R4.P$2, R9.Pin_1, J1.A3
  N9: R5.P$2, R6.Pin_1, J1.A4/SDA#114
  N10: R6.Pin_0, R10.Pin_0, J1.5V#1187
  N11: D1.C, J1.A5/SCL
  N12: D2.C, J1.A4/SDA#1159
  N13: D4.C, J1.D13/SCK
  N14: D5.C, J1.D12/MISO
  N15: J1.5V#338, J3.Vcc
  N16: J1.D4, J3.Vout
  N17: J1.D5_PWM, J2.Vout
  N18: J1.D6_PWM, J4.Vout
  N19: J1.PB5, U2.VIN
  N20: J1.PA3, U2.VOUT
  N21: J1.GND#3328, J3.GND
  N22: U1.B, U2.GND
